// Logisim project LC-3 (1).circ as structural Verilog: 15 circuits, main circuit main
module main (
);

  wire clock_1_out, controlunit_1_alucontrol, controlunit_1_memread, controlunit_1_memwrite,
       controlunit_1_mux1, controlunit_1_mux3, controlunit_1_mux4, controlunit_1_mux5, controlunit_1_pcread,
       controlunit_1_pcwrite, controlunit_1_we;
  wire [1:0] controlunit_1_mux2;
  wire [2:0] controlunit_1_rd1, controlunit_1_rd2, controlunit_1_wr;
  wire [15:0] _4_0__S_extent_p2, _8_0__Z_extent_out_2, adder_1_out, adder_2_out, alu_1_aluout,
       multiplexer_1_out, multiplexer_2_out, multiplexer_3_out, multiplexer_4_out, multiplexer_5_out,
       pc_1_output, ram_1_data, Register_File_outdata1, Register_File_outdata2;
  wire [17:0] _8_0__S_Extent_out_2, rom_1_data;

  Clock clock_1 (.out(clock_1_out));
  PC pc_1 (
    .\input (multiplexer_5_out), .en(controlunit_1_pcread), .clk(clock_1_out), .write(controlunit_1_pcwrite),
    .\output (pc_1_output));
  Adder #(.width(16)) adder_1 (.a(pc_1_output), .b(16'h1), .out(adder_1_out), .cin(1'b0));  // open: cout
  ROM #(.addrWidth(10), .dataWidth(18)) rom_1 (.addr(pc_1_output[9:0]), .data(rom_1_data), .sel(1'b1));
  registerFile Register_File (
    .rd1(controlunit_1_rd1), .rd2(controlunit_1_rd2), .inData(multiplexer_3_out), .Wr(controlunit_1_wr),
    .clk(clock_1_out), .WE(controlunit_1_we), .outData2(Register_File_outdata2),
    .outData1(Register_File_outdata1));
  // SignExtent5 _4_0__S_extent: pin names not known; wires that end beside it: rom_1_data, _4_0__S_extent_p2
  SignExtent6 _8_0__S_Extent (.in_1(rom_1_data), .out_2(_8_0__S_Extent_out_2));
  ZeroExtent9 _8_0__Z_extent (.in_1(rom_1_data[15:0]), .out_2(_8_0__Z_extent_out_2));
  // _16_Bit_Register_File 16_bit_register_file_1: pin names not known
  ControlUnit controlunit_1 (
    .CU_input(rom_1_data[15:0]), .rd2(controlunit_1_rd2), .rd1(controlunit_1_rd1), .Wr(controlunit_1_wr),
    .clk(clock_1_out), .Mux1(controlunit_1_mux1), .Mux2(controlunit_1_mux2), .Mux3(controlunit_1_mux3),
    .Mux4(controlunit_1_mux4), .Mux5(controlunit_1_mux5), .MemRead(controlunit_1_memread),
    .ALUcontrol(controlunit_1_alucontrol), .WE(controlunit_1_we), .MemWrite(controlunit_1_memwrite),
    .PCwrite(controlunit_1_pcwrite), .PCread(controlunit_1_pcread));  // open: InstrRead
  Multiplexer #(.width(16), .enable("false")) multiplexer_1 (
    .in0(Register_File_outdata2), .in1(_4_0__S_extent_p2), .out(multiplexer_1_out), .sel(controlunit_1_mux1));
  Adder #(.width(16)) adder_2 (.a(_8_0__Z_extent_out_2), .b(adder_1_out), .out(adder_2_out), .cin(1'b0));  // open: cout
  ALU alu_1 (
    .input1(Register_File_outdata1), .input2(multiplexer_1_out), .ALUcontrol(controlunit_1_alucontrol),
    .ALUout(alu_1_aluout));
  Multiplexer #(.select(2), .width(16), .enable("false")) multiplexer_2 (
    .in0(alu_1_aluout), .in1(_8_0__Z_extent_out_2), .in2(adder_2_out), .in3(_8_0__S_Extent_out_2[15:0]),
    .out(multiplexer_2_out), .sel(controlunit_1_mux2));
  RAM #(.addrWidth(16), .dataWidth(16), .bus("separate")) ram_1 (
    .addr(multiplexer_2_out), .din(Register_File_outdata2), .data(ram_1_data), .str(controlunit_1_memwrite),
    .sel(1'b1), .clk(clock_1_out), .ld(controlunit_1_memread), .clr(1'b0));
  Multiplexer #(.width(16), .enable("false")) multiplexer_3 (
    .in0(multiplexer_4_out), .in1(adder_1_out), .out(multiplexer_3_out), .sel(controlunit_1_mux4));
  Multiplexer #(.width(16), .enable("false")) multiplexer_4 (
    .in0(ram_1_data), .in1(multiplexer_2_out), .out(multiplexer_4_out), .sel(controlunit_1_mux3));
  Multiplexer #(.width(16), .enable("false")) multiplexer_5 (
    .in0(multiplexer_4_out), .in1(adder_1_out), .out(multiplexer_5_out), .sel(controlunit_1_mux5));
  // Pins of 16 and 18 bits meet at rom_1_data
  // Pins of 10 and 16 bits meet at pc_1_output
  // Pins of 16 and 18 bits meet at _8_0__S_Extent_out_2

  // Notes on the sheet:
  //   Instruction Memory
  //   contents of rom_1 (hex, n*v repeats v):
  //   5408 5808 5c04 9c04 1c00f 2c0a0 2540c 20c0c d47c 10878 172ff 1b73e 159a0 247e0 8c0 380c0 3c0b0
  //   Data Memory
endmodule

module SignExtent6 (
  input  [17:0] in_1,
  output [17:0] out_2
);

  assign out_2 = {{12{in_1[5]}}, in_1[5:0]};  // Bit_Extender bit_extender_1
endmodule

module ZeroExtent9 (
  input  [15:0] in_1,
  output [15:0] out_2
);


  assign out_2 = {{7{1'b0}}, in_1[8:0]};
endmodule

module ZeroExtent8 (
  input  [15:0] in_1,
  output [15:0] out_2
);


  assign out_2 = {{8{1'b0}}, in_1[7:0]};
endmodule

module SignExtent5 (
  input  [17:0] in_1,
  input  [7:0] in_2,
  output [17:0] out_3,
  output [15:0] out_4
);

  assign out_4 = {{8{1'b0}}, in_2};  // Bit_Extender bit_extender_1

  assign out_3 = {{12{in_1[6]}}, in_1[5:0]};
endmodule

module ALU (
  input  ALUcontrol,
  input  [15:0] input1,
  input  [15:0] input2,
  output [15:0] ALUout
);

  wire not_1_out;
  wire [15:0] adder_1_out, and_1_out;

  Adder #(.width(16)) adder_1 (.a(input1), .b(input2), .out(adder_1_out));  // open: cin, cout
  not not_1 (not_1_out, ALUcontrol);
  assign and_1_out = input1 & input2;  // AND_Gate and_1, 16 bits wide
  assign ALUout = ALUcontrol ? adder_1_out : 16'bz;  // Controlled_Buffer controlled_buffer_1
  assign ALUout = not_1_out ? and_1_out : 16'bz;  // Controlled_Buffer controlled_buffer_2
endmodule

// Control Unit
module ControlUnit (
  input  [15:0] CU_input,
  input  clk,
  output Mux1,
  output [1:0] Mux2,
  output Mux3,
  output Mux4,
  output Mux5,
  output MemRead,
  output ALUcontrol,
  output WE,
  output [2:0] rd2,
  output MemWrite,
  output [2:0] rd1,
  output [2:0] Wr,
  output PCwrite,
  output InstrRead,
  output PCread
);

  wire and_1_out, and_2_out, decoder_1_out0, decoder_1_out1, decoder_1_out2, decoder_1_out4, decoder_1_out5,
       not_1_out, not_2_out, not_3_out, not_4_out, or_1_out, register_1_q;
  wire [3:0] counter_1_q;

  assign rd1 = and_1_out ? CU_input[11:9] : 3'bz;  // Controlled_Buffer controlled_buffer_1
  not not_1 (not_1_out, and_1_out);
  assign rd1 = not_1_out ? CU_input[8:6] : 3'bz;  // Controlled_Buffer controlled_buffer_2
  and and_1 (and_1_out, not_2_out, not_3_out, CU_input[14], CU_input[15]);
  not not_2 (not_2_out, CU_input[12]);
  not not_3 (not_3_out, CU_input[13]);
  Counter #(.width(4), .max('hf)) counter_1 (
    .load(decoder_1_out1), .D(CU_input[15:12]), .count(or_1_out), .Q(counter_1_q), .clk(clk), .clr(and_2_out));  // open: carry
  and and_2 (and_2_out, not_4_out, register_1_q);
  not not_4 (not_4_out, or_1_out);
  or or_1 (or_1_out, decoder_1_out0, decoder_1_out4);
  Register #(.width(1)) register_1 (.D(PCwrite), .en(1'b1), .Q(register_1_q), .clk(clk), .clr(1'b0));
  Decoder #(.select(4), .enable("false")) decoder_1 (
    .out0(decoder_1_out0), .out1(decoder_1_out1), .out2(decoder_1_out2), .out4(decoder_1_out4),
    .out5(decoder_1_out5), .out8(ALUcontrol), .out10(Mux2[1]), .out12(MemWrite), .sel(counter_1_q));  // open: out3, out6, out7, out9, out11, out13, out14, out15
  or or_2 (Mux2[0], decoder_1_out5, decoder_1_out4, MemWrite, Mux2[1]);
  not not_5 (Mux5, Mux2[1]);
  or or_3 (Mux3, decoder_1_out2, Mux2[1], ALUcontrol);
  or or_4 (MemRead, decoder_1_out5, decoder_1_out4);
  or or_5 (WE, decoder_1_out2, decoder_1_out5, ALUcontrol);
  or or_6 (PCwrite, decoder_1_out5, Mux2[1], ALUcontrol, decoder_1_out2, MemWrite);

  assign InstrRead = 1'b1;
  assign Mux1 = CU_input[5];
  assign Mux4 = 1'b0;
  assign PCread = 1'b1;
  assign rd2 = CU_input[2:0];
  assign Wr = CU_input[11:9];

  // Notes on the sheet:
  //   Fetch1
  //   Fetch2
  //   AND1
  //   LD1
  //   LD2
  //   ADD1
  //   JMP1
  //   ST1
endmodule

module PC (
  input  write,
  input  [15:0] \input ,
  input  en,
  input  clk,
  output [15:0] \output 
);

  wire [15:0] multiplexer_1_out;

  Multiplexer #(.width(16), .enable("false")) multiplexer_1 (
    .in0(\output ), .in1(\input ), .out(multiplexer_1_out), .sel(write));
  Register #(.width(16)) register_1 (.D(multiplexer_1_out), .en(en), .Q(\output ), .clk(clk), .clr(1'b0));
endmodule

// Read Register 1
module _18BitRegisterFile (
  input  [3:0] Read_Register_1,
  input  [3:0] Read_Register_1_2,
  input  [3:0] Write_Register_1,
  input  [17:0] in_4,
  input  clk,
  input  clk_2,
  output [17:0] Register_1_Output,
  output [17:0] Register_2_Output
);

  wire and_1_out, and_2_out, and_3_out, and_4_out, and_5_out, and_6_out, and_7_out, and_8_out, and_9_out,
       and_10_out, and_11_out, and_12_out, and_13_out, and_14_out, and_15_out, and_16_out, decoder_1_out0,
       decoder_1_out1, decoder_1_out2, decoder_1_out3, decoder_1_out4, decoder_1_out5, decoder_1_out6,
       decoder_1_out7, decoder_1_out8, decoder_1_out9, decoder_1_out10, decoder_1_out11, decoder_1_out12,
       decoder_1_out13, decoder_1_out14, decoder_1_out15, decoder_2_out0, decoder_2_out1, decoder_2_out2,
       decoder_2_out3, decoder_2_out4, decoder_2_out5, decoder_2_out6, decoder_2_out7, decoder_2_out8,
       decoder_2_out9, decoder_2_out10, decoder_2_out11, decoder_2_out12, decoder_2_out13, decoder_2_out14,
       decoder_2_out15, decoder_3_out0, decoder_3_out1, decoder_3_out2, decoder_3_out3, decoder_3_out4,
       decoder_3_out5, decoder_3_out6, decoder_3_out7, decoder_3_out8, decoder_3_out9, decoder_3_out10,
       decoder_3_out11, decoder_3_out12, decoder_3_out13, decoder_3_out14, decoder_3_out15, undriven;
  wire [17:0] register_1_q, register_2_q, register_3_q, register_4_q, register_5_q, register_6_q,
       register_7_q, register_8_q, register_9_q, register_10_q, register_11_q, register_12_q, register_13_q,
       register_14_q, register_15_q, register_16_q;

  Decoder #(.select(4), .enable("false")) decoder_1 (
    .out0(decoder_1_out0), .out1(decoder_1_out1), .out2(decoder_1_out2), .out3(decoder_1_out3),
    .out4(decoder_1_out4), .out5(decoder_1_out5), .out6(decoder_1_out6), .out7(decoder_1_out7),
    .out8(decoder_1_out8), .out9(decoder_1_out9), .out10(decoder_1_out10), .out11(decoder_1_out11),
    .out12(decoder_1_out12), .out13(decoder_1_out13), .out14(decoder_1_out14), .out15(decoder_1_out15),
    .sel(Read_Register_1_2));
  Decoder #(.select(4), .enable("false")) decoder_2 (
    .out0(decoder_2_out0), .out1(decoder_2_out1), .out2(decoder_2_out2), .out3(decoder_2_out3),
    .out4(decoder_2_out4), .out5(decoder_2_out5), .out6(decoder_2_out6), .out7(decoder_2_out7),
    .out8(decoder_2_out8), .out9(decoder_2_out9), .out10(decoder_2_out10), .out11(decoder_2_out11),
    .out12(decoder_2_out12), .out13(decoder_2_out13), .out14(decoder_2_out14), .out15(decoder_2_out15),
    .sel(Write_Register_1));
  and and_1 (and_1_out, decoder_2_out14, clk_2);
  and and_2 (and_2_out, decoder_2_out15, clk_2);
  and and_3 (and_3_out, decoder_2_out10, clk_2);
  and and_4 (and_4_out, decoder_2_out11, clk_2);
  and and_5 (and_5_out, decoder_2_out12, clk_2);
  and and_6 (and_6_out, decoder_2_out13, clk_2);
  and and_7 (and_7_out, decoder_2_out8, clk_2);
  and and_8 (and_8_out, decoder_2_out9, clk_2);
  and and_9 (and_9_out, decoder_2_out5, clk_2);
  and and_10 (and_10_out, decoder_2_out6, clk_2);
  and and_11 (and_11_out, decoder_2_out7, clk_2);
  and and_12 (and_12_out, decoder_2_out0, clk_2);
  and and_13 (and_13_out, decoder_2_out1, clk_2);
  and and_14 (and_14_out, decoder_2_out2, clk_2);
  and and_15 (and_15_out, decoder_2_out3, clk_2);
  Decoder #(.select(4), .enable("false")) decoder_3 (
    .out0(decoder_3_out0), .out1(decoder_3_out1), .out2(decoder_3_out2), .out3(decoder_3_out3),
    .out4(decoder_3_out4), .out5(decoder_3_out5), .out6(decoder_3_out6), .out7(decoder_3_out7),
    .out8(decoder_3_out8), .out9(decoder_3_out9), .out10(decoder_3_out10), .out11(decoder_3_out11),
    .out12(decoder_3_out12), .out13(decoder_3_out13), .out14(decoder_3_out14), .out15(decoder_3_out15),
    .sel(Read_Register_1));
  and and_16 (and_16_out, decoder_2_out4, clk_2);
  Register #(.width(18)) register_1 (.D(in_4), .en(and_12_out), .Q(register_1_q), .clk(clk), .clr(undriven));
  Register #(.width(18)) register_2 (.D(in_4), .en(and_13_out), .Q(register_2_q), .clk(clk), .clr(undriven));
  Register #(.width(18)) register_3 (.D(in_4), .en(and_14_out), .Q(register_3_q), .clk(clk), .clr(undriven));
  Register #(.width(18)) register_4 (.D(in_4), .en(and_15_out), .Q(register_4_q), .clk(clk), .clr(undriven));
  Register #(.width(18)) register_5 (.D(in_4), .en(and_16_out), .Q(register_5_q), .clk(clk), .clr(undriven));
  Register #(.width(18)) register_6 (.D(in_4), .en(and_9_out), .Q(register_6_q), .clk(clk), .clr(undriven));
  Register #(.width(18)) register_7 (.D(in_4), .en(and_10_out), .Q(register_7_q), .clk(clk), .clr(undriven));
  Register #(.width(18)) register_8 (.D(in_4), .en(and_11_out), .Q(register_8_q), .clk(clk), .clr(undriven));
  Register #(.width(18)) register_9 (.D(in_4), .en(and_7_out), .Q(register_9_q), .clk(clk), .clr(undriven));
  Register #(.width(18)) register_10 (.D(in_4), .en(and_8_out), .Q(register_10_q), .clk(clk), .clr(undriven));
  Register #(.width(18)) register_11 (.D(in_4), .en(and_3_out), .Q(register_11_q), .clk(clk), .clr(undriven));
  Register #(.width(18)) register_12 (.D(in_4), .en(and_4_out), .Q(register_12_q), .clk(clk), .clr(undriven));
  Register #(.width(18)) register_13 (.D(in_4), .en(and_5_out), .Q(register_13_q), .clk(clk), .clr(undriven));
  Register #(.width(18)) register_14 (.D(in_4), .en(and_6_out), .Q(register_14_q), .clk(clk), .clr(undriven));
  Register #(.width(18)) register_15 (.D(in_4), .en(and_1_out), .Q(register_15_q), .clk(clk), .clr(undriven));
  Register #(.width(18)) register_16 (.D(in_4), .en(and_2_out), .Q(register_16_q), .clk(clk), .clr(undriven));
  assign Register_1_Output = decoder_3_out13 ? register_14_q : 18'bz;  // Controlled_Buffer controlled_buffer_1
  assign Register_2_Output = decoder_1_out13 ? register_14_q : 18'bz;  // Controlled_Buffer controlled_buffer_2
  assign Register_1_Output = decoder_3_out14 ? register_15_q : 18'bz;  // Controlled_Buffer controlled_buffer_3
  assign Register_2_Output = decoder_1_out14 ? register_15_q : 18'bz;  // Controlled_Buffer controlled_buffer_4
  assign Register_1_Output = decoder_3_out15 ? register_16_q : 18'bz;  // Controlled_Buffer controlled_buffer_5
  assign Register_2_Output = decoder_1_out15 ? register_16_q : 18'bz;  // Controlled_Buffer controlled_buffer_6
  assign Register_1_Output = decoder_3_out9 ? register_10_q : 18'bz;  // Controlled_Buffer controlled_buffer_7
  assign Register_2_Output = decoder_1_out9 ? register_10_q : 18'bz;  // Controlled_Buffer controlled_buffer_8
  assign Register_1_Output = decoder_3_out10 ? register_11_q : 18'bz;  // Controlled_Buffer controlled_buffer_9
  assign Register_2_Output = decoder_1_out10 ? register_11_q : 18'bz;  // Controlled_Buffer controlled_buffer_10
  assign Register_1_Output = decoder_3_out11 ? register_12_q : 18'bz;  // Controlled_Buffer controlled_buffer_11
  assign Register_2_Output = decoder_1_out11 ? register_12_q : 18'bz;  // Controlled_Buffer controlled_buffer_12
  assign Register_1_Output = decoder_3_out12 ? register_13_q : 18'bz;  // Controlled_Buffer controlled_buffer_13
  assign Register_2_Output = decoder_1_out12 ? register_13_q : 18'bz;  // Controlled_Buffer controlled_buffer_14
  assign Register_1_Output = decoder_3_out5 ? register_6_q : 18'bz;  // Controlled_Buffer controlled_buffer_15
  assign Register_2_Output = decoder_1_out5 ? register_6_q : 18'bz;  // Controlled_Buffer controlled_buffer_16
  assign Register_1_Output = decoder_3_out6 ? register_7_q : 18'bz;  // Controlled_Buffer controlled_buffer_17
  assign Register_2_Output = decoder_1_out6 ? register_7_q : 18'bz;  // Controlled_Buffer controlled_buffer_18
  assign Register_1_Output = decoder_3_out7 ? register_8_q : 18'bz;  // Controlled_Buffer controlled_buffer_19
  assign Register_2_Output = decoder_1_out7 ? register_8_q : 18'bz;  // Controlled_Buffer controlled_buffer_20
  assign Register_1_Output = decoder_3_out8 ? register_9_q : 18'bz;  // Controlled_Buffer controlled_buffer_21
  assign Register_2_Output = decoder_1_out8 ? register_9_q : 18'bz;  // Controlled_Buffer controlled_buffer_22
  assign Register_1_Output = decoder_3_out1 ? register_2_q : 18'bz;  // Controlled_Buffer controlled_buffer_23
  assign Register_2_Output = decoder_1_out1 ? register_2_q : 18'bz;  // Controlled_Buffer controlled_buffer_24
  assign Register_1_Output = decoder_3_out2 ? register_3_q : 18'bz;  // Controlled_Buffer controlled_buffer_25
  assign Register_2_Output = decoder_1_out2 ? register_3_q : 18'bz;  // Controlled_Buffer controlled_buffer_26
  assign Register_1_Output = decoder_3_out3 ? register_4_q : 18'bz;  // Controlled_Buffer controlled_buffer_27
  assign Register_2_Output = decoder_1_out3 ? register_4_q : 18'bz;  // Controlled_Buffer controlled_buffer_28
  assign Register_1_Output = decoder_3_out4 ? register_5_q : 18'bz;  // Controlled_Buffer controlled_buffer_29
  assign Register_2_Output = decoder_1_out4 ? register_5_q : 18'bz;  // Controlled_Buffer controlled_buffer_30
  assign Register_1_Output = decoder_3_out0 ? register_1_q : 18'bz;  // Controlled_Buffer controlled_buffer_31
  assign Register_2_Output = decoder_1_out0 ? register_1_q : 18'bz;  // Controlled_Buffer controlled_buffer_32
endmodule

module registerFile (
  input  [2:0] rd1,
  input  [2:0] rd2,
  input  [15:0] inData,
  input  [2:0] Wr,
  input  WE,
  input  clk,
  output [15:0] outData2,
  output [15:0] outData1
);

  wire and_1_out, and_2_out, and_3_out, and_4_out, and_5_out, and_6_out, and_7_out, and_8_out,
       decoder_1_out0, decoder_1_out1, decoder_1_out2, decoder_1_out3, decoder_1_out4, decoder_1_out5,
       decoder_1_out6, decoder_1_out7, decoder_2_out0, decoder_2_out1, decoder_2_out2, decoder_2_out3,
       decoder_2_out4, decoder_2_out5, decoder_2_out6, decoder_2_out7, decoder_3_out0, decoder_3_out1,
       decoder_3_out2, decoder_3_out3, decoder_3_out4, decoder_3_out5, decoder_3_out6, decoder_3_out7;
  wire [15:0] register_1_q, register_2_q, register_3_q, register_4_q, register_5_q, register_6_q,
       register_7_q, register_8_q;

  Decoder #(.select(3), .enable("false")) decoder_1 (
    .out0(decoder_1_out0), .out1(decoder_1_out1), .out2(decoder_1_out2), .out3(decoder_1_out3),
    .out4(decoder_1_out4), .out5(decoder_1_out5), .out6(decoder_1_out6), .out7(decoder_1_out7), .sel(rd1));
  Decoder #(.select(3), .enable("false")) decoder_2 (
    .out0(decoder_2_out0), .out1(decoder_2_out1), .out2(decoder_2_out2), .out3(decoder_2_out3),
    .out4(decoder_2_out4), .out5(decoder_2_out5), .out6(decoder_2_out6), .out7(decoder_2_out7), .sel(Wr));
  Decoder #(.select(3), .enable("false")) decoder_3 (
    .out0(decoder_3_out0), .out1(decoder_3_out1), .out2(decoder_3_out2), .out3(decoder_3_out3),
    .out4(decoder_3_out4), .out5(decoder_3_out5), .out6(decoder_3_out6), .out7(decoder_3_out7), .sel(rd2));
  and and_1 (and_1_out, decoder_2_out0, WE);
  and and_2 (and_2_out, decoder_2_out1, WE);
  and and_3 (and_3_out, decoder_2_out2, WE);
  and and_4 (and_4_out, decoder_2_out3, WE);
  and and_5 (and_5_out, decoder_2_out4, WE);
  and and_6 (and_6_out, decoder_2_out5, WE);
  and and_7 (and_7_out, decoder_2_out6, WE);
  and and_8 (and_8_out, decoder_2_out7, WE);
  Register #(.width(16)) register_1 (.D(inData), .en(and_1_out), .Q(register_1_q), .clk(clk), .clr(1'b0));
  Register #(.width(16)) register_2 (.D(inData), .en(and_2_out), .Q(register_2_q), .clk(clk), .clr(1'b0));
  Register #(.width(16)) register_3 (.D(inData), .en(and_3_out), .Q(register_3_q), .clk(clk), .clr(1'b0));
  Register #(.width(16)) register_4 (.D(inData), .en(and_4_out), .Q(register_4_q), .clk(clk), .clr(1'b0));
  Register #(.width(16)) register_5 (.D(inData), .en(and_5_out), .Q(register_5_q), .clk(clk), .clr(1'b0));
  Register #(.width(16)) register_6 (.D(inData), .en(and_6_out), .Q(register_6_q), .clk(clk), .clr(1'b0));
  Register #(.width(16)) register_7 (.D(inData), .en(and_7_out), .Q(register_7_q), .clk(clk), .clr(1'b0));
  Register #(.width(16)) register_8 (.D(inData), .en(and_8_out), .Q(register_8_q), .clk(clk), .clr(1'b0));
  assign outData2 = decoder_3_out0 ? register_1_q : 16'bz;  // Controlled_Buffer controlled_buffer_1
  assign outData1 = decoder_1_out0 ? register_1_q : 16'bz;  // Controlled_Buffer controlled_buffer_2
  assign outData2 = decoder_3_out1 ? register_2_q : 16'bz;  // Controlled_Buffer controlled_buffer_3
  assign outData1 = decoder_1_out1 ? register_2_q : 16'bz;  // Controlled_Buffer controlled_buffer_4
  assign outData2 = decoder_3_out2 ? register_3_q : 16'bz;  // Controlled_Buffer controlled_buffer_5
  assign outData1 = decoder_1_out2 ? register_3_q : 16'bz;  // Controlled_Buffer controlled_buffer_6
  assign outData2 = decoder_3_out3 ? register_4_q : 16'bz;  // Controlled_Buffer controlled_buffer_7
  assign outData1 = decoder_1_out3 ? register_4_q : 16'bz;  // Controlled_Buffer controlled_buffer_8
  assign outData2 = decoder_3_out4 ? register_5_q : 16'bz;  // Controlled_Buffer controlled_buffer_9
  assign outData1 = decoder_1_out4 ? register_5_q : 16'bz;  // Controlled_Buffer controlled_buffer_10
  assign outData2 = decoder_3_out5 ? register_6_q : 16'bz;  // Controlled_Buffer controlled_buffer_11
  assign outData1 = decoder_1_out5 ? register_6_q : 16'bz;  // Controlled_Buffer controlled_buffer_12
  assign outData2 = decoder_3_out6 ? register_7_q : 16'bz;  // Controlled_Buffer controlled_buffer_13
  assign outData1 = decoder_1_out6 ? register_7_q : 16'bz;  // Controlled_Buffer controlled_buffer_14
  assign outData2 = decoder_3_out7 ? register_8_q : 16'bz;  // Controlled_Buffer controlled_buffer_15
  assign outData1 = decoder_1_out7 ? register_8_q : 16'bz;  // Controlled_Buffer controlled_buffer_16
endmodule

module _18BitALU (
  input  NAND,
  input  NOR,
  input  ADD,
  input  AND,
  input  [17:0] Input_1,
  input  [17:0] Input_2,
  output [17:0] out_7,
  output [17:0] out_8,
  output ZF,
  output CF
);

  wire adder_1_cout;
  wire [17:0] adder_1_out, and_1_out, nand_1_out, nor_1_out;

  assign and_1_out = Input_2 & Input_1;  // AND_Gate and_1, 18 bits wide
  Substractor substractor_1 (.in_1(Input_1), .in_2(Input_2), .out_3(out_8), .CF(CF));
  Adder #(.width(18)) adder_1 (.a(Input_1), .b(Input_2), .out(adder_1_out), .cout(adder_1_cout));  // open: cin
  assign nand_1_out = ~(Input_2 & Input_1);  // NAND_Gate nand_1, 18 bits wide
  assign nor_1_out = ~(Input_2 | Input_1);  // NOR_Gate nor_1, 18 bits wide
  assign out_7 = ADD ? adder_1_out : 18'bz;  // Controlled_Buffer controlled_buffer_1
  assign out_7 = AND ? and_1_out : 18'bz;  // Controlled_Buffer controlled_buffer_2
  assign out_7 = NAND ? nand_1_out : 18'bz;  // Controlled_Buffer controlled_buffer_3
  assign out_7 = NOR ? nor_1_out : 18'bz;  // Controlled_Buffer controlled_buffer_4
  _18bitTo1BitNorGate u_18bitto1bitnorgate_1 (.in_1(out_8), .Zero(ZF));
  // also tied to GND on the sheet: adder_1_cout
endmodule

module _18bitTo1BitNorGate (
  input  [17:0] in_1,
  output Zero
);

  nor nor_1 (Zero, in_1[0], in_1[1], in_1[2], in_1[3], in_1[4], in_1[5], in_1[6], in_1[7], in_1[8], in_1[10], in_1[11], in_1[12], in_1[13], in_1[14], in_1[15], in_1[16], in_1[17], in_1[9]);
endmodule

module Substractor (
  input  [17:0] in_1,
  input  [17:0] in_2,
  output [17:0] out_3,
  output CF
);

  wire adder_1_cout;
  wire [17:0] not_1_out;

  assign not_1_out = ~in_2;  // NOT_Gate not_1, 18 bits wide
  Adder #(.width(18)) adder_1 (.a(in_1), .b(not_1_out), .out(out_3), .cin(1'b1), .cout(adder_1_cout));
  not not_2 (CF, adder_1_cout);
endmodule

module SignExtent14 (
  input  [17:0] in_1,
  output [17:0] out_2
);

  assign out_2 = {{4{in_1[13]}}, in_1[13:0]};  // Bit_Extender bit_extender_1
endmodule

module PC18 (
  input  write,
  input  [17:0] \input ,
  input  en,
  input  clk,
  output [17:0] \output 
);

  wire [17:0] multiplexer_1_out;

  Multiplexer #(.width(18), .enable("false")) multiplexer_1 (
    .in0(\output ), .in1(\input ), .out(multiplexer_1_out), .sel(write));
  Register #(.width(18)) register_1 (.D(multiplexer_1_out), .en(en), .Q(\output ), .clk(clk), .clr(1'b0));
endmodule
