// Logisim project Processor.circ as structural Verilog: 21 circuits, main circuit main
module main (
  input  in_1
);

  wire alu, and_1_out, CLK, cmp, cmpJump, cmpJumpEnable, enableCMPJUMP, enableJUMP, enablePC, enablePCCU,
       enablePCFSM, enableWrite, jump, memRead, memWrite, nextInstruction, nextInstructionFSM, or_1_out,
       regWrite;
  wire [1:0] ALUcontrol;
  wire [3:0] DEST_SRC_OP1, multiplexer_1_out, multiplexer_3_out, SRC1_OP2, SRC2;
  wire [5:0] IMM6;
  wire [9:0] memAddress, pc18_1_out_8;
  wire [10:0] jumpAddress;
  wire [17:0] ALU1Operand, ALU2Operand, aluOutput, dataMem, memInput, multiplexer_2_out, REG2, rom_1_data;

  Clock clock_1 (.out(CLK));
  _18BitALU u_18bitalu_1 (
    .Input1(ALU1Operand), .ALUSelect(ALUcontrol), .Input2(ALU2Operand), .out_8(aluOutput), .clk(CLK),
    .alu(alu), .reset(in_1));  // open: cout
  PC18 pc18_1 (
    .cmpJump(enableCMPJUMP), .enable(enablePC), .jump(enableJUMP), .clk(CLK), .reset(in_1),
    .jumpAddress(jumpAddress), .out_8(pc18_1_out_8), .nextInstr(nextInstruction));
  // Probe on aluOutput
  Multiplexer #(.width(4), .enable("false")) multiplexer_1 (
    .in0(SRC2), .in1(SRC1_OP2), .out(multiplexer_1_out), .sel(cmp));
  Multiplexer #(.width(18), .enable("false")) multiplexer_2 (
    .in0(aluOutput), .in1(dataMem), .out(multiplexer_2_out), .sel(memRead));
  ROM #(.addrWidth(10), .dataWidth(18)) rom_1 (.addr(pc18_1_out_8), .data(rom_1_data));  // open: sel
  ControlUnit controlunit_1 (
    .instruction(rom_1_data), .CLK(CLK), .register1(memInput), .register2(REG2), .DST_SRC_OP1(DEST_SRC_OP1),
    .alu(alu), .SRC1_OP2(SRC1_OP2), .SRC2(SRC2), .regWrite(regWrite), .aluControl(ALUcontrol), .IMM6(IMM6),
    .cmpJump(cmpJump), .J_ADDR10(jumpAddress), .memRead(memRead), .memWrite(memWrite), .M_ADDR10(memAddress),
    .jump(jump), .cmp(cmp), .reset(in_1), .cmpJumpEnable(cmpJumpEnable), .enablePC(enablePCCU),
    .aluOperand1(ALU1Operand), .aluOperand2(ALU2Operand));
  or or_1 (or_1_out, cmp, memWrite);
  Multiplexer #(.width(4), .enable("false")) multiplexer_3 (
    .in0(SRC1_OP2), .in1(DEST_SRC_OP1), .out(multiplexer_3_out), .sel(or_1_out));
  and and_1 (and_1_out, regWrite, enableWrite);
  _18BitRegisterFile u_18bitregisterfile_1 (
    .Register_1_Output_bbf3fe56(memInput), .Register_2_Output_31a387df(REG2),
    .Write_Register_1_76b1a88a(DEST_SRC_OP1), .in_2(multiplexer_1_out), .writeEnable(and_1_out),
    .Read_Register_1_6b833ddc(multiplexer_3_out), .in_4(multiplexer_2_out), .clk(CLK), .reset(in_1));
  // Probe on ALU1Operand
  // Probe on ALU2Operand
  or or_2 (enablePC, enablePCCU, enablePCFSM);
  or or_3 (nextInstruction, enablePCCU, nextInstructionFSM);
  FSM fsm_1 (
    .alu(alu), .ST(memWrite), .LD(memRead), .JUMP(jump), .CMPJUMP(cmpJump), .cmpJumpEnable(cmpJumpEnable),
    .clk(CLK), .enableWrite(enableWrite), .enablePC(enablePCFSM), .enableJUMP(enableJUMP),
    .nextInstruction(nextInstructionFSM), .enableCMPJUMP(enableCMPJUMP), .reset(in_1));
  RAM #(.addrWidth(10), .dataWidth(18), .bus("separate")) ram_1 (
    .addr(memAddress), .din(memInput), .data(dataMem), .str(memWrite), .sel(1'b1), .clk(CLK), .ld(memRead));  // open: clr

  // Other names for the same wires on the sheet: REG1[17:0] = memInput; reset = in_1

  // Notes on the sheet:
  //   instruction memory
  //   contents of rom_1 (hex, n*v repeats v):
  //   16ecf 17fc5 7ffc 2afc0 33ff0
  //   Control Unit(Parsing Instruction and setting signals)
  //   FSM
endmodule

module ControlUnit (
  input  [17:0] instruction,
  input  reset,
  input  CLK,
  input  [17:0] register1,
  input  [17:0] register2,
  output alu,
  output [3:0] DST_SRC_OP1,
  output regWrite,
  output [3:0] SRC1_OP2,
  output [3:0] SRC2,
  output [1:0] aluControl,
  output [5:0] IMM6,
  output cmpJump,
  output [10:0] J_ADDR10,
  output memRead,
  output cmp,
  output [17:0] aluOperand1,
  output memWrite,
  output enablePC,
  output jump,
  output [9:0] M_ADDR10,
  output cmpJumpEnable,
  output [17:0] aluOperand2
);

  wire ADD, ADDI, AND, and_1_out, and_2_out, and_3_out, and_4_out, and_5_out, and_6_out, and_7_out,
       and_8_out, and_9_out, ANDI, CF, comparer_1_cf, comparer_1_zf, isImmediate, JA, JAE, JB, JBE, JE, NAND,
       NOR, not_1_out, not_2_out, or_2_out, ZF;
  wire [17:0] controlled_buffer_1_out, SignExtent_2_out_2, SignExtent_out_2;

  Decoder #(.select(4)) decoder_1 (
    .out1(ADD), .out2(AND), .out3(NAND), .out4(NOR), .out5(ADDI), .out6(ANDI), .out7(jump), .out8(memRead),
    .out9(memWrite), .out10(cmp), .out11(JE), .out12(JA), .out13(JB), .out14(JAE), .out15(JBE),
    .sel(instruction[17:14]), .en(1'b1));  // open: out0
  SignExtent6 SignExtent (.in_1(instruction[5:0]), .out_2(SignExtent_out_2));
  SignExtent6 SignExtent_2 (.in_1(instruction[5:0]), .out_2(SignExtent_2_out_2));
  // OR_Gate or_1 has open pins: in0=ADD, in1=ADDI, out=open
  or or_2 (or_2_out, AND, ANDI);
  or or_3 (isImmediate, ADDI, ANDI);
  assign controlled_buffer_1_out = ADDI ? SignExtent_out_2 : 18'bz;  // Controlled_Buffer controlled_buffer_1
  assign controlled_buffer_1_out = ANDI ? SignExtent_2_out_2 : 18'bz;  // Controlled_Buffer controlled_buffer_2
  or or_4 (aluControl[0], or_2_out, NOR);
  or or_5 (aluControl[1], NAND, NOR);
  Comparer comparer_1 (.Input1(register1), .Input2(register2), .ZF(comparer_1_zf), .CF(comparer_1_cf));
  DFlipFlop u_ZF (.Q(ZF), .D(comparer_1_zf), .clk(CLK), .enable(cmp), .reset(reset));
  DFlipFlop u_CF (.Q(CF), .D(comparer_1_cf), .clk(CLK), .enable(cmp), .reset(reset));
  Multiplexer #(.width(18), .enable("false")) multiplexer_1 (
    .in0(register2), .in1(controlled_buffer_1_out), .out(aluOperand2), .sel(isImmediate));
  not not_1 (not_1_out, CF);
  not not_2 (not_2_out, ZF);
  or or_6 (alu, ADD, ADDI, AND, ANDI, NAND, NOR);
  and and_1 (and_1_out, not_1_out, ZF);
  and and_2 (and_2_out, not_1_out, not_2_out);
  and and_3 (and_3_out, CF, not_2_out);
  and and_4 (and_4_out, CF, ZF);
  and and_5 (and_5_out, and_1_out, JE);
  and and_6 (and_6_out, and_2_out, JA);
  and and_7 (and_7_out, and_3_out, JB);
  and and_8 (and_8_out, not_1_out, JAE);
  and and_9 (and_9_out, and_4_out, JBE);
  or or_7 (regWrite, alu, memRead);
  or or_8 (cmpJump, JB, JAE, JE, JA, JBE);
  or or_9 (cmpJumpEnable, and_5_out, and_6_out, and_7_out, and_8_out, and_9_out);

  assign aluOperand1 = register1;
  assign DST_SRC_OP1 = instruction[13:10];
  assign enablePC = cmp;
  assign IMM6 = instruction[5:0];
  assign J_ADDR10 = instruction[13:3];
  assign M_ADDR10 = instruction[9:0];
  assign SRC1_OP2 = instruction[9:6];
  assign SRC2 = instruction[5:2];

  // Other names for the same wires on the sheet: OP2[3:0] = instruction[9:6]; SRC1[3:0] = instruction[9:6];
  //   DEST[3:0] = instruction[13:10]; OP1[3:0] = instruction[13:10]; SRC[3:0] = instruction[13:10]; LD = memRead;
  //   opcode[3:0] = instruction[17:14]; ST = memWrite

  // Notes on the sheet:
  //   ADD 00, AND 01, NAND 10, NOR 11
endmodule

// Program Counter
module PC18 (
  input  [10:0] jumpAddress,
  input  nextInstr,
  input  jump,
  input  enable,
  input  cmpJump,
  input  clk,
  input  reset,
  output [9:0] out_8
);

  wire and_1_out, or_1_out;
  wire [9:0] n10bitadder_1_out_4, n10bitadder_2_out_4, n10bitsubstractor_1_out_3, newJumpAddress,
       newPcAddress, nextInstAddress, not_1_out;

  _10BitAdder u_10bitadder_1 (
    .cin(1'b0), .input1(out_8), .input2(jumpAddress[9:0]), .out_4(n10bitadder_1_out_4));  // open: cout
  assign not_1_out = ~jumpAddress[9:0];  // NOT_Gate not_1, 10 bits wide
  _10BitAdder u_10bitadder_2 (
    .cin(1'b0), .input1(not_1_out), .input2(10'h1), .out_4(n10bitadder_2_out_4));  // open: cout
  _10BitSubstractor u_10bitsubstractor_1 (
    .in_1(out_8), .in_2(n10bitadder_2_out_4), .out_3(n10bitsubstractor_1_out_3));  // open: CF
  Multiplexer #(.width(10), .enable("false")) multiplexer_1 (
    .in0(n10bitadder_1_out_4), .in1(n10bitsubstractor_1_out_3), .out(newJumpAddress), .sel(jumpAddress[10]));
  _10BitRegister u_10bitregister_1 (
    .\input (newPcAddress), .clock(clk), .reset(reset), .\output (out_8), .enable(enable));
  _10BitAdder u_10bitadder_3 (.cin(1'b0), .input1(out_8), .input2(10'h1), .out_4(nextInstAddress));  // open: cout
  assign newPcAddress = nextInstr ? nextInstAddress : 10'bz;  // Controlled_Buffer controlled_buffer_1
  or or_1 (or_1_out, jump, cmpJump);
  assign newPcAddress = or_1_out ? newJumpAddress : 10'bz;  // Controlled_Buffer controlled_buffer_2
  and and_1 (and_1_out, ~nextInstr, ~jump, ~cmpJump);  // AND_Gate
  assign newPcAddress = and_1_out ? out_8 : 10'bz;  // Controlled_Buffer controlled_buffer_3
  // Probe on nextInstAddress
  // Probe on newPcAddress

  // Other names for the same wires on the sheet: output[9:0] = out_8

  // Notes on the sheet:
  //   if it is negative then do substracting
  //   1->jump
  //   2-> cmpJump
  //   0-> next
endmodule

module FSM (
  input  alu,
  input  ST,
  input  LD,
  input  JUMP,
  input  CMPJUMP,
  input  cmpJumpEnable,
  input  clk,
  input  reset,
  output enableWrite,
  output enablePC,
  output enableJUMP,
  output enableCMPJUMP,
  output nextInstruction
);

  wire aluPC, aluWrite, and_1_out, and_2_out, and_4_out, cmpJUMPPC, dflipflop_1_q, dflipflop_2_q,
       dflipflop_7_q, dflipflop_8_q, ldPC, ldWrite, multiplexer_3_out, multiplexer_4_out, multiplexer_5_out,
       not_1_out, not_2_out, not_3_out, not_4_out, not_5_out, not_6_out, not_7_out, not_8_out, not_9_out,
       not_10_out, not_11_out, not_12_out, not_13_out, not_14_out, not_15_out, not_16_out, or_1_out,
       or_2_out, or_3_out, or_4_out, or_5_out, or_6_out, or_7_out, or_8_out, stPC;
  wire [1:0] dflipflop_4_q, dflipflop_6_q, multiplexer_1_out, multiplexer_2_out;

  not not_1 (not_1_out, LD);
  not not_2 (not_2_out, ST);
  not not_3 (not_3_out, JUMP);
  not not_4 (not_4_out, alu);
  or or_1 (or_1_out, not_4_out, reset);
  or or_2 (or_2_out, not_1_out, reset);
  or or_3 (or_3_out, not_2_out, reset);
  or or_4 (or_4_out, not_3_out, reset);
  not not_5 (not_5_out, CMPJUMP);
  or or_5 (or_5_out, not_5_out, reset);
  Multiplexer #(.select(2), .width(2)) multiplexer_1 (
    .in0(2'b01), .in1(2'b10), .in2(2'b00), .out(multiplexer_1_out), .sel(dflipflop_4_q), .en(alu));  // open: in3
  Multiplexer #(.select(2), .width(2)) multiplexer_2 (
    .in0(2'b01), .in1(2'b10), .in2(2'b00), .out(multiplexer_2_out), .sel(dflipflop_6_q), .en(LD));  // open: in3
  Multiplexer #(.enable("false")) multiplexer_3 (.in0(1'b1), .in1(1'b0), .out(multiplexer_3_out), .sel(dflipflop_7_q));
  Multiplexer #(.enable("false")) multiplexer_4 (.in0(1'b1), .in1(1'b0), .out(multiplexer_4_out), .sel(dflipflop_1_q));
  Multiplexer #(.enable("false")) multiplexer_5 (.in0(1'b1), .in1(1'b0), .out(multiplexer_5_out), .sel(dflipflop_2_q));
  DFlipFlop dflipflop_1 (.Q(dflipflop_1_q), .D(multiplexer_4_out), .clk(clk), .enable(JUMP), .reset(or_4_out));
  DFlipFlop dflipflop_2 (.Q(dflipflop_2_q), .D(multiplexer_5_out), .clk(clk), .enable(CMPJUMP), .reset(or_5_out));
  DFlipFlop dflipflop_3 (.Q(dflipflop_4_q[1]), .D(multiplexer_1_out[1]), .clk(clk), .enable(alu), .reset(or_1_out));
  DFlipFlop dflipflop_4 (.Q(dflipflop_4_q[0]), .D(multiplexer_1_out[0]), .clk(clk), .enable(alu), .reset(or_1_out));
  DFlipFlop dflipflop_5 (.Q(dflipflop_6_q[1]), .D(multiplexer_2_out[1]), .clk(clk), .enable(LD), .reset(or_2_out));
  DFlipFlop dflipflop_6 (.Q(dflipflop_6_q[0]), .D(multiplexer_2_out[0]), .clk(clk), .enable(LD), .reset(or_2_out));
  DFlipFlop dflipflop_7 (.Q(dflipflop_7_q), .D(multiplexer_3_out), .clk(clk), .enable(ST), .reset(or_3_out));
  not not_6 (not_6_out, dflipflop_4_q[0]);
  not not_7 (not_7_out, dflipflop_4_q[1]);
  not not_8 (not_8_out, dflipflop_4_q[0]);
  assign aluWrite = not_8_out ? 1'b0 : 1'bz;  // Controlled_Buffer controlled_buffer_1
  not not_9 (not_9_out, dflipflop_6_q[0]);
  and and_1 (and_1_out, not_9_out, not_10_out);
  not not_10 (not_10_out, dflipflop_6_q[1]);
  not not_11 (not_11_out, dflipflop_6_q[0]);
  assign ldWrite = dflipflop_6_q[0] ? 1'b1 : 1'bz;  // Controlled_Buffer controlled_buffer_2
  assign ldWrite = not_11_out ? 1'b0 : 1'bz;  // Controlled_Buffer controlled_buffer_3
  not not_12 (not_12_out, dflipflop_7_q);
  assign stPC = dflipflop_7_q ? 1'b1 : 1'bz;  // Controlled_Buffer controlled_buffer_4
  not not_13 (not_13_out, dflipflop_1_q);
  assign enableJUMP = dflipflop_1_q ? 1'b1 : 1'bz;  // Controlled_Buffer controlled_buffer_5
  not not_14 (not_14_out, dflipflop_2_q);
  assign cmpJUMPPC = dflipflop_2_q ? 1'b1 : 1'bz;  // Controlled_Buffer controlled_buffer_6
  and and_2 (and_2_out, not_6_out, not_7_out);
  assign aluPC = dflipflop_4_q[1] ? 1'b1 : 1'bz;  // Controlled_Buffer controlled_buffer_7
  assign aluWrite = dflipflop_4_q[0] ? 1'b1 : 1'bz;  // Controlled_Buffer controlled_buffer_8
  or or_6 (or_6_out, and_1_out, dflipflop_6_q[0]);
  assign ldPC = or_6_out ? 1'b0 : 1'bz;  // Controlled_Buffer controlled_buffer_9
  assign ldPC = dflipflop_6_q[1] ? 1'b1 : 1'bz;  // Controlled_Buffer controlled_buffer_10
  assign stPC = not_12_out ? 1'b0 : 1'bz;  // Controlled_Buffer controlled_buffer_11
  assign enableJUMP = not_13_out ? 1'b0 : 1'bz;  // Controlled_Buffer controlled_buffer_12
  assign cmpJUMPPC = not_14_out ? 1'b0 : 1'bz;  // Controlled_Buffer controlled_buffer_13
  or or_7 (or_7_out, and_2_out, dflipflop_4_q[0]);
  assign aluPC = or_7_out ? 1'b0 : 1'bz;  // Controlled_Buffer controlled_buffer_14
  and and_3 (enableCMPJUMP, cmpJUMPPC, cmpJumpEnable);
  not not_15 (not_15_out, cmpJumpEnable);
  and and_4 (and_4_out, cmpJUMPPC, not_15_out);
  or or_8 (or_8_out, aluPC, ldPC, stPC, enableJUMP, cmpJUMPPC);
  or or_9 (nextInstruction, aluPC, ldPC, stPC, and_4_out);
  DFlipFlop dflipflop_8 (.Q(dflipflop_8_q), .D(1'b1), .clk(clk), .enable(1'b1), .reset(reset));
  not not_16 (not_16_out, dflipflop_8_q);
  or or_10 (enableWrite, aluWrite, ldWrite);
  or or_11 (enablePC, or_8_out, not_16_out);

  // Other names for the same wires on the sheet: jumpPC = enableJUMP

  // Notes on the sheet:
  //   st immediatly happens in our design
  //   no need extra state
  //   2 state
  //   0 initial
  //   1 increment pc or jump
  //   2 state
  //   0 initial
  //   1 increment pc or jump
  //   2 increment pc
  //   2 state
  //   0 initial
  //   1 increment pc
  //   3 state, 
  //   0 initial
  //   1 register write
  //   3 state, 
  //   0 initial
  //   1 register write
  //   2 increment pc
  //   ALU
  //   LD
  //   ST
  //   JUMP
  //   CMPJUMP
endmodule

module _18BitALU (
  input  [17:0] Input1,
  input  alu,
  input  reset,
  input  [1:0] ALUSelect,
  input  clk,
  input  [17:0] Input2,
  output cout,
  output [17:0] out_8
);

  wire [17:0] and_1_out, multiplexer_1_out, n18bitadder_1_out_4, nand_1_out, nor_1_out;

  _18BitAdder u_18bitadder_1 (.cout(cout), .out_4(n18bitadder_1_out_4), .A(Input1), .B(Input2), .cin(1'b0));
  assign and_1_out = Input1 & Input2;  // AND_Gate and_1, 18 bits wide
  assign nand_1_out = ~(Input1 & Input2);  // NAND_Gate nand_1, 18 bits wide
  assign nor_1_out = ~(Input1 | Input2);  // NOR_Gate nor_1, 18 bits wide
  Multiplexer #(.select(2), .width(18), .enable("false")) multiplexer_1 (
    .in0(n18bitadder_1_out_4), .in1(and_1_out), .in2(nand_1_out), .in3(nor_1_out), .out(multiplexer_1_out),
    .sel(ALUSelect));
  // Probe on multiplexer_1_out
  _18BitRegister u_18bitregister_1 (
    .\output (out_8), .\input (multiplexer_1_out), .clock(clk), .enable(alu), .reset(reset));
endmodule

module _18BitRegisterFile (
  input  [3:0] Read_Register_1_6b833ddc,
  input  [3:0] in_2,
  input  [3:0] Write_Register_1_76b1a88a,
  input  [17:0] in_4,
  input  reset,
  input  clk,
  input  writeEnable,
  output [17:0] Register_1_Output_bbf3fe56,
  output [17:0] Register_2_Output_31a387df
);

  wire and_1_out, and_2_out, and_3_out, and_4_out, and_5_out, and_6_out, and_7_out, and_8_out, and_9_out,
       and_10_out, and_11_out, and_12_out, and_13_out, and_14_out, and_15_out, and_16_out, decoder_1_out0,
       decoder_1_out1, decoder_1_out2, decoder_1_out3, decoder_1_out4, decoder_1_out5, decoder_1_out6,
       decoder_1_out7, decoder_1_out8, decoder_1_out9, decoder_1_out10, decoder_1_out11, decoder_1_out12,
       decoder_1_out13, decoder_1_out14, decoder_1_out15, decoder_2_out0, decoder_2_out1, decoder_2_out2,
       decoder_2_out3, decoder_2_out4, decoder_2_out5, decoder_2_out6, decoder_2_out7, decoder_2_out8,
       decoder_2_out9, decoder_2_out10, decoder_2_out11, decoder_2_out12, decoder_2_out13, decoder_2_out14,
       decoder_2_out15, decoder_3_out0, decoder_3_out1, decoder_3_out2, decoder_3_out3, decoder_3_out4,
       decoder_3_out5, decoder_3_out6, decoder_3_out7, decoder_3_out8, decoder_3_out9, decoder_3_out10,
       decoder_3_out11, decoder_3_out12, decoder_3_out13, decoder_3_out14, decoder_3_out15;
  wire [17:0] n18bitregister_1_output, n18bitregister_2_output, n18bitregister_3_output,
       n18bitregister_4_output, n18bitregister_5_output, n18bitregister_6_output, n18bitregister_7_output,
       n18bitregister_8_output, n18bitregister_9_output, n18bitregister_10_output, n18bitregister_11_output,
       n18bitregister_12_output, n18bitregister_13_output, n18bitregister_14_output,
       n18bitregister_15_output, n18bitregister_16_output;

  Decoder #(.select(4), .enable("false")) decoder_1 (
    .out0(decoder_1_out0), .out1(decoder_1_out1), .out2(decoder_1_out2), .out3(decoder_1_out3),
    .out4(decoder_1_out4), .out5(decoder_1_out5), .out6(decoder_1_out6), .out7(decoder_1_out7),
    .out8(decoder_1_out8), .out9(decoder_1_out9), .out10(decoder_1_out10), .out11(decoder_1_out11),
    .out12(decoder_1_out12), .out13(decoder_1_out13), .out14(decoder_1_out14), .out15(decoder_1_out15),
    .sel(in_2));
  Decoder #(.select(4), .enable("false")) decoder_2 (
    .out0(decoder_2_out0), .out1(decoder_2_out1), .out2(decoder_2_out2), .out3(decoder_2_out3),
    .out4(decoder_2_out4), .out5(decoder_2_out5), .out6(decoder_2_out6), .out7(decoder_2_out7),
    .out8(decoder_2_out8), .out9(decoder_2_out9), .out10(decoder_2_out10), .out11(decoder_2_out11),
    .out12(decoder_2_out12), .out13(decoder_2_out13), .out14(decoder_2_out14), .out15(decoder_2_out15),
    .sel(Write_Register_1_76b1a88a));
  and and_1 (and_1_out, decoder_2_out14, writeEnable);
  and and_2 (and_2_out, decoder_2_out15, writeEnable);
  and and_3 (and_3_out, decoder_2_out10, writeEnable);
  and and_4 (and_4_out, decoder_2_out11, writeEnable);
  and and_5 (and_5_out, decoder_2_out12, writeEnable);
  and and_6 (and_6_out, decoder_2_out13, writeEnable);
  and and_7 (and_7_out, decoder_2_out8, writeEnable);
  and and_8 (and_8_out, decoder_2_out9, writeEnable);
  and and_9 (and_9_out, decoder_2_out5, writeEnable);
  and and_10 (and_10_out, decoder_2_out6, writeEnable);
  and and_11 (and_11_out, decoder_2_out7, writeEnable);
  and and_12 (and_12_out, decoder_2_out0, writeEnable);
  and and_13 (and_13_out, decoder_2_out1, writeEnable);
  and and_14 (and_14_out, decoder_2_out2, writeEnable);
  and and_15 (and_15_out, decoder_2_out3, writeEnable);
  Decoder #(.select(4), .enable("false")) decoder_3 (
    .out0(decoder_3_out0), .out1(decoder_3_out1), .out2(decoder_3_out2), .out3(decoder_3_out3),
    .out4(decoder_3_out4), .out5(decoder_3_out5), .out6(decoder_3_out6), .out7(decoder_3_out7),
    .out8(decoder_3_out8), .out9(decoder_3_out9), .out10(decoder_3_out10), .out11(decoder_3_out11),
    .out12(decoder_3_out12), .out13(decoder_3_out13), .out14(decoder_3_out14), .out15(decoder_3_out15),
    .sel(Read_Register_1_6b833ddc));
  and and_16 (and_16_out, decoder_2_out4, writeEnable);
  _18BitRegister u_18bitregister_1 (
    .\output (n18bitregister_1_output), .\input (in_4), .clock(clk), .enable(and_12_out), .reset(reset));
  _18BitRegister u_18bitregister_2 (
    .\output (n18bitregister_2_output), .\input (in_4), .clock(clk), .enable(and_13_out), .reset(reset));
  _18BitRegister u_18bitregister_3 (
    .\output (n18bitregister_3_output), .\input (in_4), .clock(clk), .enable(and_14_out), .reset(reset));
  _18BitRegister u_18bitregister_4 (
    .\output (n18bitregister_4_output), .\input (in_4), .clock(clk), .enable(and_15_out), .reset(reset));
  _18BitRegister u_18bitregister_5 (
    .\output (n18bitregister_5_output), .\input (in_4), .clock(clk), .enable(and_16_out), .reset(reset));
  _18BitRegister u_18bitregister_6 (
    .\output (n18bitregister_6_output), .\input (in_4), .clock(clk), .enable(and_9_out), .reset(reset));
  _18BitRegister u_18bitregister_7 (
    .\output (n18bitregister_7_output), .\input (in_4), .clock(clk), .enable(and_10_out), .reset(reset));
  _18BitRegister u_18bitregister_8 (
    .\output (n18bitregister_8_output), .\input (in_4), .clock(clk), .enable(and_11_out), .reset(reset));
  _18BitRegister u_18bitregister_9 (
    .\output (n18bitregister_9_output), .\input (in_4), .clock(clk), .enable(and_7_out), .reset(reset));
  _18BitRegister u_18bitregister_10 (
    .\output (n18bitregister_10_output), .\input (in_4), .clock(clk), .enable(and_8_out), .reset(reset));
  _18BitRegister u_18bitregister_11 (
    .\output (n18bitregister_11_output), .\input (in_4), .clock(clk), .enable(and_3_out), .reset(reset));
  _18BitRegister u_18bitregister_12 (
    .\output (n18bitregister_12_output), .\input (in_4), .clock(clk), .enable(and_4_out), .reset(reset));
  _18BitRegister u_18bitregister_13 (
    .\output (n18bitregister_13_output), .\input (in_4), .clock(clk), .enable(and_5_out), .reset(reset));
  _18BitRegister u_18bitregister_14 (
    .\output (n18bitregister_14_output), .\input (in_4), .clock(clk), .enable(and_6_out), .reset(reset));
  _18BitRegister u_18bitregister_15 (
    .\output (n18bitregister_15_output), .\input (in_4), .clock(clk), .enable(and_1_out), .reset(reset));
  _18BitRegister u_18bitregister_16 (
    .\output (n18bitregister_16_output), .\input (in_4), .clock(clk), .enable(and_2_out), .reset(reset));
  assign Register_1_Output_bbf3fe56 = decoder_3_out13 ? n18bitregister_14_output : 18'bz;  // Controlled_Buffer controlled_buffer_1
  assign Register_2_Output_31a387df = decoder_1_out13 ? n18bitregister_14_output : 18'bz;  // Controlled_Buffer controlled_buffer_2
  assign Register_1_Output_bbf3fe56 = decoder_3_out14 ? n18bitregister_15_output : 18'bz;  // Controlled_Buffer controlled_buffer_3
  assign Register_2_Output_31a387df = decoder_1_out14 ? n18bitregister_15_output : 18'bz;  // Controlled_Buffer controlled_buffer_4
  assign Register_1_Output_bbf3fe56 = decoder_3_out15 ? n18bitregister_16_output : 18'bz;  // Controlled_Buffer controlled_buffer_5
  assign Register_2_Output_31a387df = decoder_1_out15 ? n18bitregister_16_output : 18'bz;  // Controlled_Buffer controlled_buffer_6
  assign Register_1_Output_bbf3fe56 = decoder_3_out9 ? n18bitregister_10_output : 18'bz;  // Controlled_Buffer controlled_buffer_7
  assign Register_2_Output_31a387df = decoder_1_out9 ? n18bitregister_10_output : 18'bz;  // Controlled_Buffer controlled_buffer_8
  assign Register_1_Output_bbf3fe56 = decoder_3_out10 ? n18bitregister_11_output : 18'bz;  // Controlled_Buffer controlled_buffer_9
  assign Register_2_Output_31a387df = decoder_1_out10 ? n18bitregister_11_output : 18'bz;  // Controlled_Buffer controlled_buffer_10
  assign Register_1_Output_bbf3fe56 = decoder_3_out11 ? n18bitregister_12_output : 18'bz;  // Controlled_Buffer controlled_buffer_11
  assign Register_2_Output_31a387df = decoder_1_out11 ? n18bitregister_12_output : 18'bz;  // Controlled_Buffer controlled_buffer_12
  assign Register_1_Output_bbf3fe56 = decoder_3_out12 ? n18bitregister_13_output : 18'bz;  // Controlled_Buffer controlled_buffer_13
  assign Register_2_Output_31a387df = decoder_1_out12 ? n18bitregister_13_output : 18'bz;  // Controlled_Buffer controlled_buffer_14
  assign Register_1_Output_bbf3fe56 = decoder_3_out5 ? n18bitregister_6_output : 18'bz;  // Controlled_Buffer controlled_buffer_15
  assign Register_2_Output_31a387df = decoder_1_out5 ? n18bitregister_6_output : 18'bz;  // Controlled_Buffer controlled_buffer_16
  assign Register_1_Output_bbf3fe56 = decoder_3_out6 ? n18bitregister_7_output : 18'bz;  // Controlled_Buffer controlled_buffer_17
  assign Register_2_Output_31a387df = decoder_1_out6 ? n18bitregister_7_output : 18'bz;  // Controlled_Buffer controlled_buffer_18
  assign Register_1_Output_bbf3fe56 = decoder_3_out7 ? n18bitregister_8_output : 18'bz;  // Controlled_Buffer controlled_buffer_19
  assign Register_2_Output_31a387df = decoder_1_out7 ? n18bitregister_8_output : 18'bz;  // Controlled_Buffer controlled_buffer_20
  assign Register_1_Output_bbf3fe56 = decoder_3_out8 ? n18bitregister_9_output : 18'bz;  // Controlled_Buffer controlled_buffer_21
  assign Register_2_Output_31a387df = decoder_1_out8 ? n18bitregister_9_output : 18'bz;  // Controlled_Buffer controlled_buffer_22
  assign Register_1_Output_bbf3fe56 = decoder_3_out1 ? n18bitregister_2_output : 18'bz;  // Controlled_Buffer controlled_buffer_23
  assign Register_2_Output_31a387df = decoder_1_out1 ? n18bitregister_2_output : 18'bz;  // Controlled_Buffer controlled_buffer_24
  assign Register_1_Output_bbf3fe56 = decoder_3_out2 ? n18bitregister_3_output : 18'bz;  // Controlled_Buffer controlled_buffer_25
  assign Register_2_Output_31a387df = decoder_1_out2 ? n18bitregister_3_output : 18'bz;  // Controlled_Buffer controlled_buffer_26
  assign Register_1_Output_bbf3fe56 = decoder_3_out3 ? n18bitregister_4_output : 18'bz;  // Controlled_Buffer controlled_buffer_27
  assign Register_2_Output_31a387df = decoder_1_out3 ? n18bitregister_4_output : 18'bz;  // Controlled_Buffer controlled_buffer_28
  assign Register_1_Output_bbf3fe56 = decoder_3_out4 ? n18bitregister_5_output : 18'bz;  // Controlled_Buffer controlled_buffer_29
  assign Register_2_Output_31a387df = decoder_1_out4 ? n18bitregister_5_output : 18'bz;  // Controlled_Buffer controlled_buffer_30
  assign Register_1_Output_bbf3fe56 = decoder_3_out0 ? n18bitregister_1_output : 18'bz;  // Controlled_Buffer controlled_buffer_31
  assign Register_2_Output_31a387df = decoder_1_out0 ? n18bitregister_1_output : 18'bz;  // Controlled_Buffer controlled_buffer_32
endmodule

module _18BitRegister (
  input  [17:0] \input ,
  input  clock,
  input  enable,
  input  reset,
  output [17:0] \output 
);

  DFlipFlop dflipflop_1 (.Q(\output [0]), .D(\input [0]), .clk(clock), .enable(enable), .reset(reset));
  DFlipFlop dflipflop_2 (.Q(\output [1]), .D(\input [1]), .clk(clock), .enable(enable), .reset(reset));
  DFlipFlop dflipflop_3 (.Q(\output [2]), .D(\input [2]), .clk(clock), .enable(enable), .reset(reset));
  DFlipFlop dflipflop_4 (.Q(\output [3]), .D(\input [3]), .clk(clock), .enable(enable), .reset(reset));
  DFlipFlop dflipflop_5 (.Q(\output [4]), .D(\input [4]), .clk(clock), .enable(enable), .reset(reset));
  DFlipFlop dflipflop_6 (.Q(\output [5]), .D(\input [5]), .clk(clock), .enable(enable), .reset(reset));
  DFlipFlop dflipflop_7 (.Q(\output [6]), .D(\input [6]), .clk(clock), .enable(enable), .reset(reset));
  DFlipFlop dflipflop_8 (.Q(\output [7]), .D(\input [7]), .clk(clock), .enable(enable), .reset(reset));
  DFlipFlop dflipflop_9 (.Q(\output [8]), .D(\input [8]), .clk(clock), .enable(enable), .reset(reset));
  DFlipFlop dflipflop_10 (.Q(\output [9]), .D(\input [9]), .clk(clock), .enable(enable), .reset(reset));
  DFlipFlop dflipflop_11 (.Q(\output [10]), .D(\input [10]), .clk(clock), .enable(enable), .reset(reset));
  DFlipFlop dflipflop_12 (.Q(\output [11]), .D(\input [11]), .clk(clock), .enable(enable), .reset(reset));
  DFlipFlop dflipflop_13 (.Q(\output [12]), .D(\input [12]), .clk(clock), .enable(enable), .reset(reset));
  DFlipFlop dflipflop_14 (.Q(\output [13]), .D(\input [13]), .clk(clock), .enable(enable), .reset(reset));
  DFlipFlop dflipflop_15 (.Q(\output [14]), .D(\input [14]), .clk(clock), .enable(enable), .reset(reset));
  DFlipFlop dflipflop_16 (.Q(\output [15]), .D(\input [15]), .clk(clock), .enable(enable), .reset(reset));
  DFlipFlop dflipflop_17 (.Q(\output [16]), .D(\input [16]), .clk(clock), .enable(enable), .reset(reset));
  DFlipFlop dflipflop_18 (.Q(\output [17]), .D(\input [17]), .clk(clock), .enable(enable), .reset(reset));
endmodule

module DLatch (
  input  reset,
  input  D,
  input  enable,
  output Q
);

  wire multiplexer_1_out, multiplexer_2_out, nand_1_out, nand_2_out, nand_4_out, not_1_out;

  not not_1 (not_1_out, D);
  nand nand_1 (nand_1_out, D, enable);
  nand nand_2 (nand_2_out, enable, not_1_out);
  Multiplexer #(.enable("false")) multiplexer_1 (.in0(nand_1_out), .in1(1'b1), .out(multiplexer_1_out), .sel(reset));
  Multiplexer #(.enable("false")) multiplexer_2 (.in0(nand_2_out), .in1(1'b0), .out(multiplexer_2_out), .sel(reset));
  nand nand_3 (Q, multiplexer_1_out, nand_4_out);
  nand nand_4 (nand_4_out, Q, multiplexer_2_out);
endmodule

module DFlipFlop (
  input  reset,
  input  D,
  input  clk,
  input  enable,
  output Q
);

  wire and_1_out, and_2_out, Master_q, not_1_out, not_2_out;

  not not_1 (not_1_out, clk);
  and and_1 (and_1_out, not_1_out, enable);
  not not_2 (not_2_out, not_1_out);
  and and_2 (and_2_out, not_2_out, enable);
  DLatch Master (.Q(Master_q), .D(D), .enable(and_1_out), .reset(reset));
  DLatch Slave (.Q(Q), .D(Master_q), .enable(and_2_out), .reset(reset));
endmodule

module Substractor (
  input  [17:0] in_1,
  input  [17:0] in_2,
  output [17:0] out_3,
  output CF
);

  wire n18bitadder_1_cout;
  wire [17:0] not_1_out;

  assign not_1_out = ~in_2;  // NOT_Gate not_1, 18 bits wide
  // Probe on not_1_out
  _18BitAdder u_18bitadder_1 (.cout(n18bitadder_1_cout), .out_4(out_3), .A(in_1), .B(not_1_out), .cin(1'b1));
  not not_2 (CF, n18bitadder_1_cout);
endmodule

module _18BitAdder (
  input  cin,
  input  [17:0] A,
  input  [17:0] B,
  output [17:0] out_4,
  output cout
);

  wire n2bitadder_1_cout, n2bitadder_2_cout, n2bitadder_3_cout, n2bitadder_4_cout, n2bitadder_5_cout,
       n2bitadder_6_cout, n2bitadder_7_cout, n2bitadder_8_cout;

  _2BitAdder u_2bitadder_1 (.cout(n2bitadder_1_cout), .out_4(out_4[1:0]), .A(A[1:0]), .B(B[1:0]), .cin(cin));
  _2BitAdder u_2bitadder_2 (
    .cout(n2bitadder_2_cout), .out_4(out_4[3:2]), .A(A[3:2]), .B(B[3:2]), .cin(n2bitadder_1_cout));
  _2BitAdder u_2bitadder_3 (
    .cout(n2bitadder_3_cout), .out_4(out_4[5:4]), .A(A[5:4]), .B(B[5:4]), .cin(n2bitadder_2_cout));
  _2BitAdder u_2bitadder_4 (
    .cout(n2bitadder_4_cout), .out_4(out_4[7:6]), .A(A[7:6]), .B(B[7:6]), .cin(n2bitadder_3_cout));
  _2BitAdder u_2bitadder_5 (
    .cout(n2bitadder_5_cout), .out_4(out_4[9:8]), .A(A[9:8]), .B(B[9:8]), .cin(n2bitadder_4_cout));
  _2BitAdder u_2bitadder_6 (
    .cout(n2bitadder_6_cout), .out_4(out_4[11:10]), .A(A[11:10]), .B(B[11:10]), .cin(n2bitadder_5_cout));
  _2BitAdder u_2bitadder_7 (
    .cout(n2bitadder_7_cout), .out_4(out_4[13:12]), .A(A[13:12]), .B(B[13:12]), .cin(n2bitadder_6_cout));
  _2BitAdder u_2bitadder_8 (
    .cout(n2bitadder_8_cout), .out_4(out_4[15:14]), .A(A[15:14]), .B(B[15:14]), .cin(n2bitadder_7_cout));
  _2BitAdder u_2bitadder_9 (.cout(cout), .out_4(out_4[17:16]), .A(A[17:16]), .B(B[17:16]), .cin(n2bitadder_8_cout));
endmodule

module _2BitAdder (
  input  cin,
  input  [1:0] A,
  input  [1:0] B,
  output [1:0] out_4,
  output cout
);

  wire n1bitadder_1_cout;

  _1BitAdder u_1bitadder_1 (.sum(out_4[0]), .cout(n1bitadder_1_cout), .A(A[0]), .B(B[0]), .cin(cin));
  _1BitAdder u_1bitadder_2 (.sum(out_4[1]), .cout(cout), .A(A[1]), .B(B[1]), .cin(n1bitadder_1_cout));

  // Notes on the sheet:
  //   cin: pull=up
endmodule

module _1BitAdder (
  input  A,
  input  B,
  input  cin,
  output sum,
  output cout
);

  wire and_1_out, and_2_out, xor_1_out;

  xor xor_1 (xor_1_out, A, B);
  and and_1 (and_1_out, B, A);
  xor xor_2 (sum, xor_1_out, cin);
  and and_2 (and_2_out, cin, xor_1_out);
  or or_1 (cout, and_2_out, and_1_out);
endmodule

module SignExtent6 (
  input  [5:0] in_1,
  output [17:0] out_2
);


  assign out_2 = {{13{in_1[5]}}, in_1[4:0]};
endmodule

module _18BitNORGate (
  input  [17:0] in_1,
  output out_2
);

  nor nor_1 (out_2, in_1[0], in_1[1], in_1[2], in_1[3], in_1[4], in_1[5], in_1[6], in_1[7], in_1[8], in_1[10], in_1[11], in_1[12], in_1[13], in_1[14], in_1[15], in_1[16], in_1[17], in_1[9]);
endmodule

module Comparer (
  input  [17:0] Input1,
  input  [17:0] Input2,
  output ZF,
  output CF
);

  wire [17:0] substractor_1_out_3;

  Substractor substractor_1 (.CF(CF), .out_3(substractor_1_out_3), .in_1(Input1), .in_2(Input2));
  _18BitNORGate u_18bitnorgate_1 (.in_1(substractor_1_out_3), .out_2(ZF));
endmodule

module ZeroExtent6 (
  input  [5:0] in_1,
  output [17:0] out_2
);


  assign out_2 = {{12{1'b0}}, in_1};
endmodule

module _1BitRegister (
  input  clk,
  input  D,
  input  reset,
  input  enable
);

  wire dflipflop_1_q, nand_1_out;

  DFlipFlop dflipflop_1 (.Q(dflipflop_1_q), .D(D), .clk(clk), .enable(enable));  // open: reset
  nand nand_1 (nand_1_out, dflipflop_1_q, reset);
endmodule

module _10BitAdder (
  input  cin,
  input  [9:0] input1,
  input  [9:0] input2,
  output [9:0] out_4,
  output cout
);

  wire n2bitadder_1_cout, n2bitadder_2_cout, n2bitadder_3_cout, n2bitadder_4_cout;

  _2BitAdder u_2bitadder_1 (.cout(n2bitadder_1_cout), .out_4(out_4[1:0]), .A(input1[1:0]), .B(input2[1:0]), .cin(cin));
  _2BitAdder u_2bitadder_2 (
    .cout(n2bitadder_2_cout), .out_4(out_4[3:2]), .A(input1[3:2]), .B(input2[3:2]), .cin(n2bitadder_1_cout));
  _2BitAdder u_2bitadder_3 (
    .cout(n2bitadder_3_cout), .out_4(out_4[5:4]), .A(input1[5:4]), .B(input2[5:4]), .cin(n2bitadder_2_cout));
  _2BitAdder u_2bitadder_4 (
    .cout(n2bitadder_4_cout), .out_4(out_4[7:6]), .A(input1[7:6]), .B(input2[7:6]), .cin(n2bitadder_3_cout));
  _2BitAdder u_2bitadder_5 (.cout(cout), .out_4(out_4[9:8]), .A(input1[9:8]), .B(input2[9:8]), .cin(n2bitadder_4_cout));
endmodule

module _10BitRegister (
  input  [9:0] \input ,
  input  clock,
  input  enable,
  input  reset,
  output [9:0] \output 
);

  DFlipFlop dflipflop_1 (.Q(\output [0]), .D(\input [0]), .clk(clock), .enable(enable), .reset(reset));
  DFlipFlop dflipflop_2 (.Q(\output [1]), .D(\input [1]), .clk(clock), .enable(enable), .reset(reset));
  DFlipFlop dflipflop_3 (.Q(\output [2]), .D(\input [2]), .clk(clock), .enable(enable), .reset(reset));
  DFlipFlop dflipflop_4 (.Q(\output [3]), .D(\input [3]), .clk(clock), .enable(enable), .reset(reset));
  DFlipFlop dflipflop_5 (.Q(\output [4]), .D(\input [4]), .clk(clock), .enable(enable), .reset(reset));
  DFlipFlop dflipflop_6 (.Q(\output [5]), .D(\input [5]), .clk(clock), .enable(enable), .reset(reset));
  DFlipFlop dflipflop_7 (.Q(\output [6]), .D(\input [6]), .clk(clock), .enable(enable), .reset(reset));
  DFlipFlop dflipflop_8 (.Q(\output [7]), .D(\input [7]), .clk(clock), .enable(enable), .reset(reset));
  DFlipFlop dflipflop_9 (.Q(\output [8]), .D(\input [8]), .clk(clock), .enable(enable), .reset(reset));
  DFlipFlop dflipflop_10 (.Q(\output [9]), .D(\input [9]), .clk(clock), .enable(enable), .reset(reset));
endmodule

module _10BitSubstractor (
  input  [9:0] in_1,
  input  [9:0] in_2,
  output [9:0] out_3,
  output CF
);

  wire n10bitadder_1_cout;
  wire [9:0] not_1_out;

  assign not_1_out = ~in_2;  // NOT_Gate not_1, 10 bits wide
  _10BitAdder u_10bitadder_1 (.cin(1'b1), .input1(in_1), .input2(not_1_out), .out_4(out_3), .cout(n10bitadder_1_cout));
  not not_2 (CF, n10bitadder_1_cout);
endmodule
